# Fritzing sketch Ultra_Sound_with_3_Led (saved by Fritzing 0.9.9b)
breadboards: 1

parts:
  Part1 = Arduino Nano (Rev3.0)
  LED1 = LED - 5mm [color="Yellow (595nm)" current=0.030 package="5 mm [THT]"]
  LED2 = LED - 5mm [color="Red (633nm)" current=0.030 package="5 mm [THT]"]
  LED3 = LED - 5mm [color="Green (570nm)" current=0.030 package="5 mm [THT]"]
  R1 = Resistor [tolerance=±5% power=0.25 resistance=220 package=THT]
  R2 = Resistor [tolerance=±5% power=0.25 resistance=220 package=THT]
  R3 = Resistor [tolerance=±5% power=0.25 resistance=220 package=THT]
  U1 = HC-SR04 [chip_label=IC package="SIP (Single Inline) [THT]"]

nets:
  GND: Part1.GND, R1.Pin_1, R2.Pin_1, R3.Pin_1, U1.GND
  N1: Part1.D2, LED2.anode
  N2: Part1.D3, LED1.anode
  N3: Part1.D4, LED3.anode
  N4: Part1.D9, U1.Trig
  N5: Part1.D10, U1.Echo
  5V: Part1.5V, U1.Vcc
  N6: LED1.cathode, R3.Pin_0
  N7: LED2.cathode, R2.Pin_0
  N8: LED3.cathode, R1.Pin_0

custom parts:
  HC-SR04: HC-SR04 ultrasound distance sensor
